// Logisim project 2to1Selector.circ as structural Verilog: 1 circuit, main circuit main
module main (
  input  B,
  input  Select,
  input  A,
  output out_4
);

  wire and_1_out, and_2_out, not_1_out;

  not not_1 (not_1_out, Select);
  and and_1 (and_1_out, B, Select);
  and and_2 (and_2_out, A, not_1_out);
  or or_1 (out_4, and_1_out, and_2_out);
endmodule
