// Logisim project 8bitlatch.circ as structural Verilog: 1 circuit, main circuit main
module main (
  input  [7:0] in_1,
  input  [7:0] in_2
);

  wire clock_1_out;

  Clock clock_1 (.out(clock_1_out));
  dtypeflipflop_main main_1 (.Hold(clock_1_out), .Data(in_1[7]), .Q(in_2[7]));  // open: Qbar
  dtypeflipflop_main main_2 (.Hold(clock_1_out), .Data(in_1[6]), .Q(in_2[6]));  // open: Qbar
  dtypeflipflop_main main_3 (.Hold(clock_1_out), .Data(in_1[5]), .Q(in_2[5]));  // open: Qbar
  dtypeflipflop_main main_4 (.Hold(clock_1_out), .Data(in_1[3]), .Q(in_2[3]));  // open: Qbar
  dtypeflipflop_main main_5 (.Hold(clock_1_out), .Data(in_1[4]), .Q(in_2[4]));  // open: Qbar
  dtypeflipflop_main main_6 (.Hold(clock_1_out), .Data(in_1[2]), .Q(in_2[2]));  // open: Qbar
  dtypeflipflop_main main_7 (.Hold(clock_1_out), .Data(in_1[1]), .Q(in_2[1]));  // open: Qbar
  dtypeflipflop_main main_8 (.Hold(clock_1_out), .Data(in_1[0]), .Q(in_2[0]));  // open: Qbar
endmodule
