// Logisim project AddingMachine.circ as structural Verilog: 1 circuit, main circuit main
module main (
  input  in_1,
  input  in_2,
  input  in_3,
  input  in_4,
  input  in_5,
  input  in_6,
  input  in_7,
  input  in_8,
  input  Select,
  input  in_10,
  input  in_11,
  input  in_12,
  input  in_13,
  input  in_14,
  input  in_15,
  input  in_16,
  input  in_17,
  input  CarryIn,
  output CarryOut
);

  wire clock_1_out, main_1_q, main_2_out_4, main_3_out_4, main_4_q, main_5_out_4, main_6_out_4, main_6_out_5,
       main_7_q, main_8_q, main_9_out_4, main_10_out_4, main_11_out_4, main_11_out_5, main_12_q,
       main_13_out_4, main_14_out_4, main_14_out_5, main_15_out_5, main_16_q, main_17_out_4, main_18_out_4,
       main_18_out_5, main_19_q, main_20_q, main_21_out_4, main_22_out_4, main_23_out_4, main_23_out_5,
       main_24_out_4, main_24_out_5;

  Clock clock_1 (.out(clock_1_out));
  dtypeflipflop_main main_1 (.Hold(clock_1_out), .Data(main_3_out_4), .Q(main_1_q));  // open: Qbar
  _2to1Selector_main main_2 (.B(main_1_q), .Select(Select), .A(in_1), .out_4(main_2_out_4));
  fulladder_main main_3 (
    .in_1(main_6_out_5), .in_2(main_2_out_4), .in_3(in_10), .out_4(main_3_out_4), .out_5(CarryOut));
  dtypeflipflop_main main_4 (.Hold(clock_1_out), .Data(main_6_out_4), .Q(main_4_q));  // open: Qbar
  _2to1Selector_main main_5 (.B(main_4_q), .Select(Select), .A(in_2), .out_4(main_5_out_4));
  fulladder_main main_6 (
    .in_1(main_11_out_5), .in_2(main_5_out_4), .in_3(in_11), .out_4(main_6_out_4), .out_5(main_6_out_5));
  dtypeflipflop_main main_7 (.Hold(clock_1_out), .Data(Select), .Q(main_7_q));  // open: Qbar
  dtypeflipflop_main main_8 (.Hold(clock_1_out), .Data(main_11_out_4), .Q(main_8_q));  // open: Qbar
  _2to1Selector_main main_9 (.B(main_8_q), .Select(Select), .A(in_3), .out_4(main_9_out_4));
  _2to1Selector_main main_10 (.B(main_7_q), .Select(Select), .A(in_4), .out_4(main_10_out_4));
  fulladder_main main_11 (
    .in_1(main_15_out_5), .in_2(main_9_out_4), .in_3(in_12), .out_4(main_11_out_4), .out_5(main_11_out_5));
  dtypeflipflop_main main_12 (.Hold(clock_1_out), .Data(main_14_out_4), .Q(main_12_q));  // open: Qbar
  _2to1Selector_main main_13 (.B(main_12_q), .Select(Select), .A(in_5), .out_4(main_13_out_4));
  fulladder_main main_14 (
    .in_1(main_18_out_5), .in_2(main_13_out_4), .in_3(in_14), .out_4(main_14_out_4), .out_5(main_14_out_5));
  fulladder_main main_15 (
    .in_1(main_14_out_5), .in_2(main_10_out_4), .in_3(in_13), .out_4(Select), .out_5(main_15_out_5));
  dtypeflipflop_main main_16 (.Hold(clock_1_out), .Data(main_18_out_4), .Q(main_16_q));  // open: Qbar
  _2to1Selector_main main_17 (.B(main_16_q), .Select(Select), .A(in_6), .out_4(main_17_out_4));
  fulladder_main main_18 (
    .in_1(main_23_out_5), .in_2(main_17_out_4), .in_3(in_15), .out_4(main_18_out_4), .out_5(main_18_out_5));
  dtypeflipflop_main main_19 (.Hold(clock_1_out), .Data(main_23_out_4), .Q(main_19_q));  // open: Qbar
  dtypeflipflop_main main_20 (.Hold(clock_1_out), .Data(main_24_out_4), .Q(main_20_q));  // open: Qbar
  _2to1Selector_main main_21 (.B(main_20_q), .Select(Select), .A(in_8), .out_4(main_21_out_4));
  _2to1Selector_main main_22 (.B(main_19_q), .Select(Select), .A(in_7), .out_4(main_22_out_4));
  fulladder_main main_23 (
    .in_1(main_24_out_5), .in_2(main_22_out_4), .in_3(in_16), .out_4(main_23_out_4), .out_5(main_23_out_5));
  fulladder_main main_24 (
    .in_1(CarryIn), .in_2(main_21_out_4), .in_3(in_17), .out_4(main_24_out_4), .out_5(main_24_out_5));
endmodule
