// Logisim project addsubtract.circ as structural Verilog: 1 circuit, main circuit main
module main (
  input  in_1,
  input  in_2,
  input  in_3,
  input  in_4,
  input  in_5,
  input  in_6,
  input  in_7,
  input  in_8,
  input  in_9,
  input  in_10,
  input  in_11,
  input  in_12,
  input  in_13,
  input  in_14,
  input  in_15,
  input  in_16,
  input  in_17,
  output [7:0] out_18
);

  wire main_1_out_5, main_2_out_5, main_3_out_5, main_4_out_5, main_5_out_5, main_6_out_5, main_7_out_5,
       main_8_out_5, nor_1_out, nor_3_out, nor_4_out, nor_5_out, nor_6_out, nor_7_out, nor_8_out, nor_9_out,
       not_1_out;

  not not_1 (not_1_out, in_1);
  nor nor_1 (nor_1_out, in_4, not_1_out);
  fulladder_main main_1 (.in_1(main_2_out_5), .in_2(in_10), .in_3(nor_1_out), .out_4(out_18[7]), .out_5(main_1_out_5));
  // NOR_Gate nor_2 has open pins: in0=main_1_out_5, in1=not_1_out, out=open
  nor nor_3 (nor_3_out, not_1_out, in_5);
  fulladder_main main_2 (.in_1(main_3_out_5), .in_2(in_13), .in_3(nor_3_out), .out_4(out_18[6]), .out_5(main_2_out_5));
  nor nor_4 (nor_4_out, not_1_out, in_8);
  fulladder_main main_3 (.in_1(main_4_out_5), .in_2(in_15), .in_3(nor_4_out), .out_4(out_18[5]), .out_5(main_3_out_5));
  nor nor_5 (nor_5_out, not_1_out, in_9);
  nor nor_6 (nor_6_out, not_1_out, in_7);
  fulladder_main main_4 (.in_1(main_5_out_5), .in_2(in_16), .in_3(nor_5_out), .out_4(out_18[4]), .out_5(main_4_out_5));
  nor nor_7 (nor_7_out, not_1_out, in_6);
  fulladder_main main_5 (.in_1(main_6_out_5), .in_2(in_17), .in_3(nor_6_out), .out_4(out_18[3]), .out_5(main_5_out_5));
  nor nor_8 (nor_8_out, not_1_out, in_3);
  fulladder_main main_6 (.in_1(main_7_out_5), .in_2(in_14), .in_3(nor_7_out), .out_4(out_18[2]), .out_5(main_6_out_5));
  nor nor_9 (nor_9_out, not_1_out, in_2);
  fulladder_main main_7 (.in_1(main_8_out_5), .in_2(in_12), .in_3(nor_8_out), .out_4(out_18[1]), .out_5(main_7_out_5));
  fulladder_main main_8 (.in_1(not_1_out), .in_2(in_11), .in_3(nor_9_out), .out_4(out_18[0]), .out_5(main_8_out_5));
endmodule
