// Logisim project dtypeflipflop.circ as structural Verilog: 1 circuit, main circuit main
module main (
  input  Hold,
  input  Data,
  output Q,
  output Qbar
);

  wire and_1_out, and_2_out, not_1_out;

  not not_1 (not_1_out, Data);
  and and_1 (and_1_out, not_1_out, Hold);
  and and_2 (and_2_out, Hold, Data);
  nor nor_1 (Q, and_1_out, Qbar);
  nor nor_2 (Qbar, Q, and_2_out);
endmodule
