// Logisim project edgetriggereddtypelipflop.circ as structural Verilog: 1 circuit, main circuit main
module main (
  input  Data,
  input  Clock,
  output Q,
  output Qbar
);

  wire and_1_out, and_2_out, and_3_out, and_4_out, nor_1_out, nor_2_out, not_1_out, not_2_out;

  not not_1 (not_1_out, Clock);
  not not_2 (not_2_out, Data);
  and and_1 (and_1_out, Data, not_1_out);
  and and_2 (and_2_out, not_1_out, not_2_out);
  nor nor_1 (nor_1_out, and_1_out, nor_2_out);
  nor nor_2 (nor_2_out, nor_1_out, and_2_out);
  and and_3 (and_3_out, nor_1_out, Clock);
  and and_4 (and_4_out, Clock, nor_2_out);
  nor nor_3 (Q, and_3_out, Qbar);
  nor nor_4 (Qbar, Q, and_4_out);
endmodule
