// Logisim project 2to1Select.circ as structural Verilog: 1 circuit, main circuit main
module main (
  input  B,
  input  Select,
  input  A,
  output Out
);

  wire and_1_out, and_2_out, not_1_out;

  not not_1 (not_1_out, Select);
  and and_1 (and_1_out, B, Select);
  and and_2 (and_2_out, not_1_out, A);
  or or_1 (Out, and_1_out, and_2_out);
endmodule
