// Logisim project 8bitadder.circ as structural Verilog: 1 circuit, main circuit main
module main (
  input  [7:0] in_1,
  input  [7:0] in_2,
  input  Carry_in,
  output Carry_Out,
  output [7:0] out_5
);

  wire main_2_out_10;

  fba_main main_1 (
    .out_10(Carry_Out), .in_1(in_2[7]), .in_2(in_2[6]), .in_3(in_2[5]), .in_4(in_2[4]), .in_5(in_2[3]),
    .in_6(in_2[2]), .in_7(in_2[1]), .in_8(in_2[0]), .out_11(out_5[7]), .out_12(out_5[6]), .out_13(out_5[5]),
    .out_14(out_5[4]), .in_9(main_2_out_10));
  fba_main main_2 (
    .out_10(main_2_out_10), .in_1(in_1[7]), .in_2(in_1[6]), .in_3(in_1[5]), .in_4(in_1[4]), .in_5(in_1[3]),
    .in_6(in_1[2]), .in_7(in_1[1]), .in_8(in_1[0]), .out_11(out_5[3]), .out_12(out_5[2]), .out_13(out_5[1]),
    .out_14(out_5[0]), .in_9(Carry_in));
endmodule
