// Logisim project 8bitlatch.circ as structural Verilog: 1 circuit, main circuit main
module main (
  input  [7:0] in_1
);

  wire clock_1_out;

  Clock clock_1 (.out(clock_1_out));
  // RSflipflop_main main_1: pin names not known
  // RSflipflop_main main_2: pin names not known
  // RSflipflop_main main_3: pin names not known
  // RSflipflop_main main_4: pin names not known
  // RSflipflop_main main_5: pin names not known
  // RSflipflop_main main_6: pin names not known
  // RSflipflop_main main_7: pin names not known
  // RSflipflop_main main_8: pin names not known
endmodule
