// Logisim project AddingMachine.circ as structural Verilog: 1 circuit, main circuit main
module main (
  input  in_1,
  input  in_2,
  input  in_3,
  input  in_4,
  input  in_5,
  input  in_6,
  input  in_7,
  input  in_8
);

  wire [7:0] undriven, undriven_2;

  _2to1Selector_main main_1 (.B(undriven_2[7]), .A(in_3));  // open: Select, out_4
  _2to1Selector_main main_2 (.B(undriven_2[6]), .A(in_4));  // open: Select, out_4
  _2to1Selector_main main_3 (.B(undriven_2[5]), .A(in_6));  // open: Select, out_4
  _8bitlatch_main main_4 (.in_1(undriven), .in_2(undriven_2));
  _2to1Selector_main main_5 (.B(undriven_2[4]), .A(in_7));  // open: Select, out_4
  _2to1Selector_main main_6 (.B(undriven_2[3]), .A(in_8));  // open: Select, out_4
  _2to1Selector_main main_7 (.B(undriven_2[1]), .A(in_2));  // open: Select, out_4
  _2to1Selector_main main_8 (.B(undriven_2[2]), .A(in_5));  // open: Select, out_4
  _2to1Selector_main main_9 (.B(undriven_2[0]), .A(in_1));  // open: Select, out_4
endmodule
