// Logisim project dtypeflipflop.circ as structural Verilog: 1 circuit, main circuit main
module main (
  input  Data,
  output Q,
  output Qbar
);

  wire and_1_out, and_2_out, Clock_out, not_1_out;

  Clock Clock (.out(Clock_out));
  not not_1 (not_1_out, Data);
  and and_1 (and_1_out, not_1_out, Clock_out);
  and and_2 (and_2_out, Clock_out, Data);
  nor nor_1 (Q, and_1_out, Qbar);
  nor nor_2 (Qbar, Q, and_2_out);
endmodule
