// Logisim project fulladder.circ as structural Verilog: 1 circuit, main circuit main
module main (
  input  Carry_In,
  input  A,
  input  B,
  output Sum,
  output Carry_Out
);

  wire main_1_out_3, main_1_out_4, main_2_out_4;

  halfadder_main main_1 (.in_1(A), .in_2(B), .out_3(main_1_out_3), .out_4(main_1_out_4));
  halfadder_main main_2 (.in_1(Carry_In), .in_2(main_1_out_3), .out_3(Sum), .out_4(main_2_out_4));
  or or_1 (Carry_Out, main_2_out_4, main_1_out_4);
endmodule
