// Logisim project halfadder.circ as structural Verilog: 1 circuit, main circuit main
module main (
  input  A,
  input  B,
  output Sum,
  output CO
);

  xor xor_1 (Sum, A, B);
  and and_1 (CO, A, B);
endmodule
